# Fritzing sketch SVF_POT_Test (saved by Fritzing 0.9.3b)
breadboards: 1

parts:
  IC1 = Dual Op-Amp [package=dip08]
  R1 = Resistor [tolerance=±5% resistance=1k package=THT]
  R3 = Resistor [tolerance=±5% resistance=10k package=THT]
  IC2 = Dual Op-Amp [package=dip08]
  C1 = Ceramic Capacitor [capacitance=100nF package="100 mil [THT, multilayer]"]
  IC3 = Dual Op-Amp [package=dip08]
  C2 = Ceramic Capacitor [capacitance=100nF package="100 mil [THT, multilayer]"]
  R6 = Resistor [tolerance=±5% resistance=10k package=THT]
  R7 = Rotary Potentiometer (Small) [maximum_resistance=100kΩ package=THT]
  R8 = Rotary Potentiometer (Small) [maximum_resistance=100kΩ package=THT]
  R9 = Rotary Potentiometer (Small) [maximum_resistance=100kΩ package=THT]

nets:
  N1: IC1.A_OUT, R3.Pin_1
  N2: IC1.A_-IN, R3.Pin_0, R6.Pin_0
  N3: IC1.A_+IN, R1.Pin_1, R7.wiper, R7.leg2
  N4: IC1.A_V-, IC2.A_V-, IC3.A_V-
  N5: IC1.B_+IN, IC2.A_+IN, IC2.B_+IN, IC3.A_+IN, IC3.B_+IN
  N6: IC1.B_-IN, IC1.B_OUT
  N7: IC1.A_V+, IC2.A_V+, IC3.A_V+
  N8: IC2.A_OUT, C1.0, R7.leg1, R9.wiper, R9.leg2
  N9: IC2.A_-IN, C1.1, R8.leg1
  N10: IC2.B_-IN, IC2.B_OUT
  N11: IC3.A_OUT, C2.0, R6.Pin_1
  N12: IC3.A_-IN, C2.1, R9.leg1
  N13: IC3.B_-IN, IC3.B_OUT

notes:
  IN
  LP
  BP
  HP
  GND
  +5V
  -5V
  GND
  100kΩ/B x 2
  100kΩ/B
