# Fritzing sketch SVF_Test (saved by Fritzing 0.9.3b)
breadboards: 1

parts:
  IC1 = Dual Op-Amp [package=dip08]
  R1 = Resistor [tolerance=±5% resistance=1k package=THT]
  R2 = Resistor [tolerance=±5% resistance=20k package=THT]
  R3 = Resistor [tolerance=±5% resistance=10k package=THT]
  IC2 = Dual Op-Amp [package=dip08]
  R4 = Resistor [tolerance=±5% resistance=16k package=THT]
  C1 = Ceramic Capacitor [capacitance=100nF package="100 mil [THT, multilayer]"]
  IC3 = Dual Op-Amp [package=dip08]
  R5 = Resistor [tolerance=±5% resistance=16k package=THT]
  C2 = Ceramic Capacitor [capacitance=100nF package="100 mil [THT, multilayer]"]
  R6 = Resistor [tolerance=±5% resistance=10k package=THT]

nets:
  N1: IC1.A_OUT, R3.Pin_1, R4.Pin_0
  N2: IC1.A_-IN, R3.Pin_0, R6.Pin_0
  N3: IC1.A_+IN, R1.Pin_1, R2.Pin_0
  N4: IC1.A_V-, IC2.A_V-, IC3.A_V-
  N5: IC1.B_+IN, IC2.A_+IN, IC2.B_+IN, IC3.A_+IN, IC3.B_+IN
  N6: IC1.B_-IN, IC1.B_OUT
  N7: IC1.A_V+, IC2.A_V+, IC3.A_V+
  N8: R2.Pin_1, IC2.A_OUT, C1.0, R5.Pin_0
  N9: IC2.A_-IN, R4.Pin_1, C1.1
  N10: IC2.B_-IN, IC2.B_OUT
  N11: IC3.A_OUT, C2.0, R6.Pin_1
  N12: IC3.A_-IN, R5.Pin_1, C2.1
  N13: IC3.B_-IN, IC3.B_OUT

notes:
  IN
  LP
  BP
  HP
  GND
  +5V
  -5V
  GND
