# Fritzing sketch SVF_AC_Coupling_PotControl_2 (saved by Fritzing 0.9.3b)
breadboards: 2

parts:
  R1 = Resistor [tolerance=±5% resistance=1k package=THT]
  R3 = Resistor [tolerance=±5% resistance=10k package=THT]
  IC2 = Dual Op-Amp [package=dip08]
  IC3 = Dual Op-Amp [package=dip08]
  R6 = Resistor [tolerance=±5% resistance=10k package=THT]
  U3 = mystery part, 3 pins [chip_label=2426]
  C4 = Electrolytic Capacitor [capacitance=1µF package="100 mil [THT, electrolytic]"]
  C5 = Electrolytic Capacitor [capacitance=1µF package="100 mil [THT, electrolytic]"]
  C6 = Electrolytic Capacitor [capacitance=1µF package="100 mil [THT, electrolytic]"]
  R9 = TRIMPOT [package=3362u-2]
  C7 = Film/Foil Capacitor [capacitance=100nF voltage=35V package="5mm [THT, pp]"]
  R10 = Resistor [tolerance=±5% resistance=100k package=THT]
  C8 = Film/Foil Capacitor [capacitance=100nF voltage=35V package="5mm [THT, pp]"]
  C9 = Film/Foil Capacitor [capacitance=100nF voltage=35V package="5mm [THT, pp]"]
  R14 = Rotary Potentiometer (Small) [maximum_resistance=100kΩ package=THT]
  R15 = Rotary Potentiometer (Small) [maximum_resistance=100kΩ package=THT]
  R16 = Rotary Potentiometer (Small) [maximum_resistance=100kΩ package=THT]
  R17 = Resistor [tolerance=±5% resistance=220 package=THT]

nets:
  N1: R1.Pin_0, C7.+, R10.Pin_0
  N2: R1.Pin_1, IC2.A_+IN, R16.wiper, R16.leg2
  N3: R3.Pin_0, IC2.A_OUT, R14.leg1, R14.wiper
  N4: R3.Pin_1, IC2.A_-IN, R6.Pin_0
  N5: IC2.A_V-, IC3.A_V-, U3.pin2, C5.-, C6.-
  N6: IC2.B_+IN, IC3.A_+IN, IC3.B_+IN, U3.pin1, C4.-, C5.+, R9.CCW, R10.Pin_1
  N7: IC2.B_-IN, C8.+, R14.leg2
  N8: IC2.B_OUT, C8.-, R15.leg2, R17.Pin_0
  N9: IC2.A_V+, IC3.A_V+, U3.pin3, C4.+, C6.+
  N10: IC3.A_OUT, R6.Pin_1, C9.-
  N11: IC3.A_-IN, C9.+, R15.leg1, R15.wiper
  N12: IC3.B_-IN, IC3.B_OUT
  N13: R9.WIPER, C7.-
  N14: R16.leg1, R17.Pin_1

notes:
  IN
  LP
  BP
  HP
  VGND
  +5V
  GND
  VGND
  +5V
  GND
  VGND
  GND
  cutoff
  100k/B x 2
  Q
  100k/B
