# Fritzing sketch SVF_AD8304_AC_Coupling (saved by Fritzing 0.9.3b)
breadboards: 3

parts:
  R1 = Resistor [tolerance=±5% resistance=1k package=THT]
  R3 = Resistor [tolerance=±5% resistance=10k package=THT]
  IC2 = Dual Op-Amp [package=dip08]
  IC3 = Dual Op-Amp [package=dip08]
  R6 = Resistor [tolerance=±5% resistance=10k package=THT]
  パーツ2 = Arduino Uno (Rev3)
  U2 = mystery part, 24 pins [chip_label=AD8403]
  C3 = Ceramic Capacitor [capacitance=100nF package="100 mil [THT, multilayer]"]
  U3 = mystery part, 3 pins [chip_label=2426]
  C4 = Electrolytic Capacitor [capacitance=1µF package="100 mil [THT, electrolytic]"]
  C5 = Electrolytic Capacitor [capacitance=1µF package="100 mil [THT, electrolytic]"]
  C6 = Electrolytic Capacitor [capacitance=1µF package="100 mil [THT, electrolytic]"]
  R7 = Rotary Potentiometer (Small) [maximum_resistance=100kΩ package=THT]
  R8 = Rotary Potentiometer (Small) [maximum_resistance=100kΩ package=THT]
  R9 = TRIMPOT [package=3362u-2]
  C7 = Film/Foil Capacitor [capacitance=100nF voltage=35V package="5mm [THT, pp]"]
  R10 = Resistor [tolerance=±5% resistance=100k package=THT]
  C8 = Film/Foil Capacitor [capacitance=100nF voltage=35V package="5mm [THT, pp]"]
  C9 = Film/Foil Capacitor [capacitance=100nF voltage=35V package="5mm [THT, pp]"]
  R11 = Resistor [tolerance=±5% resistance=2.2k package=THT]

nets:
  N1: R1.Pin_0, C7.+, R10.Pin_0
  N2: R1.Pin_1, IC2.A_+IN, U2.pin3, U2.pin4
  N3: R3.Pin_0, IC2.A_OUT, U2.pin24
  N4: R3.Pin_1, IC2.A_-IN, R6.Pin_0
  N5: IC2.A_V-, IC3.A_V-, U2.pin1, U2.pin5, U2.pin9, U2.pin17, U2.pin21, C3.1, U3.pin2, C5.-, C6.-, R7.leg1, R8.leg1
  N6: IC2.B_+IN, IC3.A_+IN, IC3.B_+IN, U3.pin1, C4.-, C5.+, R9.CCW, R10.Pin_1
  N7: IC2.B_-IN, U2.pin22, U2.pin23, C8.+
  N8: IC2.B_OUT, U2.pin18, U2.pin19, C8.-, R11.Pin_0
  N9: IC2.A_V+, IC3.A_V+, U2.pin10, U2.pin15, U2.pin16, C3.0, U3.pin3, C4.+, C6.+, R7.leg2, R8.leg2
  N10: IC3.A_OUT, R6.Pin_1, C9.-
  N11: IC3.A_-IN, U2.pin20, C9.+
  N12: IC3.B_-IN, IC3.B_OUT
  N13: パーツ2.A0, R8.wiper
  N14: パーツ2.A1, R7.wiper
  N15: パーツ2.D10_PWM/SS, U2.pin11
  N16: パーツ2.D12/MISO, U2.pin12
  N17: パーツ2.D13/SCK, U2.pin14
  N18: U2.pin2, R11.Pin_1
  N19: R9.WIPER, C7.-

notes:
  IN
  LP
  BP
  HP
  VGND
  +5V
  GND
  VGND
  AD8403
  1:AGND2 24:B1
  2:B2 23:A1
  3:A2 22:W1
  4:W2 21:AGND1
  5:AGND4 20:B3
  6:B4 19:A3
  7:A4 18:W3
  8:W4 17:AGND3
  9:DGND 16:VDD
  10:!SHDN 15:!RS
  11:!CS 14:CLK
  12:SDI 13:SDO
  GND
  +5V
  +5V
  GND
  VGND
  GND
